// Logisim project cpu_mc.circ as structural Verilog: 1 circuit, main circuit main
module main (
);

  wire adder_1_cout, alu0w, alu1w, alu_flag_eq_i, alu_flag_eq_o, alu_flag_eq_wi, alu_flag_hlt_i,
       alu_flag_hlt_o, alu_flag_ov_i, alu_flag_ov_o, alu_flag_ov_wi, and_1_out, and_2_out, and_4_out,
       and_5_out, and_6_out, and_7_out, button_2_out, clk, clock_1_out, demultiplexer_1_out0,
       demultiplexer_1_out1, demultiplexer_1_out2, demultiplexer_1_out3, demultiplexer_1_out4,
       demultiplexer_1_out5, demultiplexer_1_out6, demultiplexer_1_out7, demultiplexer_1_out8,
       demultiplexer_1_out9, demultiplexer_1_out10, demultiplexer_1_out11, demultiplexer_1_out12,
       demultiplexer_1_out13, demultiplexer_1_out14, demultiplexer_1_out15, demultiplexer_2_out0,
       demultiplexer_2_out1, demultiplexer_2_out2, demultiplexer_2_out3, demultiplexer_2_out4,
       demultiplexer_2_out5, demultiplexer_2_out6, demultiplexer_2_out7, demultiplexer_2_out8,
       demultiplexer_2_out9, demultiplexer_2_out10, demultiplexer_2_out11, demultiplexer_2_out12,
       demultiplexer_2_out13, demultiplexer_2_out14, demultiplexer_2_out15, io_save, MC_ALU_ADD,
       MC_ALU_ADD_OV, MC_ALU_AND, MC_ALU_FLAG_RES, MC_ALU_NOT, MC_ALU_OR, MC_ALU_SUB, MC_ALU_SUB_OV, MC_DONE,
       MC_IO_READ_BUS_A, MC_IO_READ_BUS_B, MC_IO_WRITE_BUS_A, MC_IO_WRITE_BUS_B, MC_JEQ, MC_JMP, MC_JNEQ,
       MC_PUT_ALU_RES_BUS, MC_PUT_REG_IOP0_HI_BUS, MC_PUT_REG_IOP0_LO_BUS, MC_PUT_VAL_IOP0_BUS,
       MC_PUT_VAL_IOP1_BUS, MC_RAM_READ_BUS_A, MC_RAM_READ_BUS_B, MC_RAM_WRITE_BUS_A, MC_RAM_WRITE_BUS_B,
       MC_STR_REG_0_BUS, MC_STR_REG_1_BUS, MC_STR_REG_2_BUS, MC_STR_REG_3_BUS, MC_STR_REG_IOP0_HI_BUS,
       MC_STR_REG_IOP0_LO_BUS, not_1_out, not_3_out, op_done, or_1_out, or_36_out, or_38_out, or_40_out,
       or_42_out, or_43_out, or_46_out, pull_resistor_7_node, pull_resistor_8_node, pull_resistor_91_node,
       ram_save, reg0w, reg1w, reg2w, reg3w, reg4w, reg5w, reg6w, reg7w, reg8w, reg9w, reg10w, reg11w,
       reg12w, reg13w, reg14w, reg15w, regwi1, regwi2, res, rip_wi, subtractor_1_bout, switch_2_p3;
  wire [3:0] regs1, regs2, rom_1_data, rom_1_data_4, rom_1_data_5, rom_1_data_6, rom_1_data_7, rom_1_data_8,
       rom_1_data_9, rom_1_data_10;
  wire [7:0] adder_1_out, alu0d, alu0o, alu1d, alu1o, alu_out, and_3_out, data_bus, demultiplexer_3_out0,
       demultiplexer_3_out1, demultiplexer_3_out2, demultiplexer_3_out3, demultiplexer_3_out4,
       demultiplexer_3_out5, demultiplexer_3_out6, demultiplexer_3_out7, demultiplexer_3_out8,
       demultiplexer_3_out9, demultiplexer_3_out10, demultiplexer_3_out11, demultiplexer_3_out12,
       demultiplexer_3_out13, demultiplexer_3_out14, demultiplexer_3_out15, demultiplexer_4_out0,
       demultiplexer_4_out1, demultiplexer_4_out2, demultiplexer_4_out3, demultiplexer_4_out4,
       demultiplexer_4_out5, demultiplexer_4_out6, demultiplexer_4_out7, demultiplexer_4_out8,
       demultiplexer_4_out9, demultiplexer_4_out10, demultiplexer_4_out11, demultiplexer_4_out12,
       demultiplexer_4_out13, demultiplexer_4_out14, demultiplexer_4_out15, io_in, io_out, not_2_out, op0,
       op1, or_41_out, ram_in, ram_out, reg0d, reg0o, reg1d, reg1o, reg2d, reg2o, reg3d, reg3o, reg4d, reg4o,
       reg5d, reg5o, reg6d, reg6o, reg7d, reg7o, reg8d, reg8o, reg9d, reg9o, reg10d, reg10o, reg11d, reg11o,
       reg12d, reg12o, reg13d, reg13o, reg14d, reg14o, reg15d, reg15o, regdi1, regdi2, regdo1, regdo2,
       rom_1_data_2, rom_1_data_3, subtractor_1_out;
  wire [15:0] io_addr, ram_addr, rip_i, rom_addr;
  wire [62:34] controlled_buffer_3_out;

  Demultiplexer #(.select(4)) demultiplexer_1 (
    .out0(demultiplexer_1_out0), .out1(demultiplexer_1_out1), .out2(demultiplexer_1_out2),
    .out3(demultiplexer_1_out3), .out4(demultiplexer_1_out4), .out5(demultiplexer_1_out5),
    .out6(demultiplexer_1_out6), .out7(demultiplexer_1_out7), .out8(demultiplexer_1_out8),
    .out9(demultiplexer_1_out9), .out10(demultiplexer_1_out10), .out11(demultiplexer_1_out11),
    .out12(demultiplexer_1_out12), .out13(demultiplexer_1_out13), .out14(demultiplexer_1_out14),
    .out15(demultiplexer_1_out15), .in(regwi1), .sel(regs1));
  Demultiplexer #(.select(4)) demultiplexer_2 (
    .out0(demultiplexer_2_out0), .out1(demultiplexer_2_out1), .out2(demultiplexer_2_out2),
    .out3(demultiplexer_2_out3), .out4(demultiplexer_2_out4), .out5(demultiplexer_2_out5),
    .out6(demultiplexer_2_out6), .out7(demultiplexer_2_out7), .out8(demultiplexer_2_out8),
    .out9(demultiplexer_2_out9), .out10(demultiplexer_2_out10), .out11(demultiplexer_2_out11),
    .out12(demultiplexer_2_out12), .out13(demultiplexer_2_out13), .out14(demultiplexer_2_out14),
    .out15(demultiplexer_2_out15), .in(regwi2), .sel(regs2));
  ROM #(.addrWidth(16), .dataWidth(64)) rom_1 (
    .addr(rom_addr),
    .data({op0, op1, rom_1_data_2, rom_1_data_3, rom_1_data, rom_1_data_4, rom_1_data_5, rom_1_data_6, rom_1_data_7, rom_1_data_8, rom_1_data_9, rom_1_data_10}));
  Button button_1 (.out(res));
  Pull_Resistor pull_resistor_1 (.node(regwi1));
  Pull_Resistor pull_resistor_2 (.node(regwi2));
  Pull_Resistor pull_resistor_3 (.node(regdi1));
  Pull_Resistor pull_resistor_4 (.node(regdi2));
  Pull_Resistor pull_resistor_5 (.node(regs1));
  Pull_Resistor pull_resistor_6 (.node(regs2));
  Pull_Resistor pull_resistor_7 (.node(pull_resistor_7_node));
  // Switch switch_1: pin names not known; wires that end beside it: 1'b1, pull_resistor_7_node
  Pull_Resistor pull_resistor_8 (.node(pull_resistor_8_node));
  // Switch switch_2: pin names not known; wires that end beside it: 1'b1, pull_resistor_8_node, switch_2_p3
  Clock clock_1 (.out(clock_1_out));
  Pull_Resistor pull_resistor_9 (.node(switch_2_p3));
  assign switch_2_p3 = pull_resistor_8_node ? clock_1_out : 1'bz;  // Controlled_Buffer controlled_buffer_1
  or or_1 (or_1_out, pull_resistor_7_node, switch_2_p3);
  not not_1 (not_1_out, alu_flag_hlt_o);
  Pull_Resistor pull_resistor_10 (.node(or_1_out));
  Pull_Resistor pull_resistor_11 (.node(clk));
  assign clk = not_1_out ? or_1_out : 1'bz;  // Controlled_Buffer controlled_buffer_2
  assign {MC_DONE, controlled_buffer_3_out, MC_JMP, alu_flag_hlt_i, MC_JNEQ, MC_JEQ, MC_PUT_ALU_RES_BUS, MC_ALU_FLAG_RES, alu_flag_eq_wi, MC_ALU_NOT, MC_ALU_OR, MC_ALU_AND, MC_ALU_SUB_OV, MC_ALU_SUB, MC_ALU_ADD_OV, MC_ALU_ADD, alu1w, alu0w, MC_IO_READ_BUS_B, MC_IO_READ_BUS_A, MC_IO_WRITE_BUS_B, MC_IO_WRITE_BUS_A, MC_RAM_READ_BUS_B, MC_RAM_READ_BUS_A, MC_RAM_WRITE_BUS_B, MC_RAM_WRITE_BUS_A, MC_STR_REG_3_BUS, MC_STR_REG_2_BUS, MC_STR_REG_1_BUS, MC_STR_REG_0_BUS, MC_PUT_VAL_IOP1_BUS, MC_PUT_VAL_IOP0_BUS, MC_STR_REG_IOP0_HI_BUS, MC_STR_REG_IOP0_LO_BUS, MC_PUT_REG_IOP0_HI_BUS, MC_PUT_REG_IOP0_LO_BUS} = and_1_out ? {op0, op1, rom_1_data_2, rom_1_data_3, rom_1_data, rom_1_data_4, rom_1_data_5, rom_1_data_6, rom_1_data_7, rom_1_data_8, rom_1_data_9, rom_1_data_10} : 64'bz;  // Controlled_Buffer controlled_buffer_3
  Pull_Resistor pull_resistor_12 (.node(MC_PUT_REG_IOP0_LO_BUS));
  Pull_Resistor pull_resistor_13 (.node(MC_PUT_REG_IOP0_HI_BUS));
  Pull_Resistor pull_resistor_14 (.node(MC_STR_REG_IOP0_LO_BUS));
  Pull_Resistor pull_resistor_15 (.node(MC_STR_REG_IOP0_HI_BUS));
  Pull_Resistor pull_resistor_16 (.node(MC_PUT_VAL_IOP0_BUS));
  Pull_Resistor pull_resistor_17 (.node(MC_PUT_VAL_IOP1_BUS));
  Pull_Resistor pull_resistor_18 (.node(MC_STR_REG_0_BUS));
  Pull_Resistor pull_resistor_19 (.node(MC_STR_REG_1_BUS));
  Pull_Resistor pull_resistor_20 (.node(MC_STR_REG_2_BUS));
  Pull_Resistor pull_resistor_21 (.node(MC_STR_REG_3_BUS));
  Pull_Resistor pull_resistor_22 (.node(MC_RAM_WRITE_BUS_A));
  Pull_Resistor pull_resistor_23 (.node(MC_RAM_WRITE_BUS_B));
  Pull_Resistor pull_resistor_24 (.node(MC_RAM_READ_BUS_A));
  Pull_Resistor pull_resistor_25 (.node(MC_RAM_READ_BUS_B));
  Pull_Resistor pull_resistor_26 (.node(MC_IO_WRITE_BUS_A));
  Pull_Resistor pull_resistor_27 (.node(MC_IO_WRITE_BUS_B));
  Pull_Resistor pull_resistor_28 (.node(MC_IO_READ_BUS_A));
  Pull_Resistor pull_resistor_29 (.node(MC_IO_READ_BUS_B));
  Pull_Resistor pull_resistor_30 (.node(alu0w));
  Pull_Resistor pull_resistor_31 (.node(alu1w));
  Pull_Resistor pull_resistor_32 (.node(MC_ALU_ADD));
  Pull_Resistor pull_resistor_33 (.node(MC_ALU_ADD_OV));
  Pull_Resistor pull_resistor_34 (.node(MC_ALU_SUB));
  Pull_Resistor pull_resistor_35 (.node(MC_ALU_SUB_OV));
  Pull_Resistor pull_resistor_36 (.node(MC_ALU_AND));
  Pull_Resistor pull_resistor_37 (.node(MC_ALU_OR));
  Pull_Resistor pull_resistor_38 (.node(MC_ALU_NOT));
  Pull_Resistor pull_resistor_39 (.node(alu_flag_eq_wi));
  Pull_Resistor pull_resistor_40 (.node(MC_ALU_FLAG_RES));
  Pull_Resistor pull_resistor_41 (.node(MC_PUT_ALU_RES_BUS));
  Pull_Resistor pull_resistor_42 (.node(MC_JEQ));
  Pull_Resistor pull_resistor_43 (.node(MC_JNEQ));
  Pull_Resistor pull_resistor_44 (.node(alu_flag_hlt_i));
  Pull_Resistor pull_resistor_45 (.node(MC_JMP));
  Pull_Resistor pull_resistor_46 (.node(controlled_buffer_3_out[34]));
  Pull_Resistor pull_resistor_47 (.node(controlled_buffer_3_out[35]));
  Pull_Resistor pull_resistor_48 (.node(controlled_buffer_3_out[36]));
  Pull_Resistor pull_resistor_49 (.node(controlled_buffer_3_out[37]));
  Pull_Resistor pull_resistor_50 (.node(controlled_buffer_3_out[38]));
  Pull_Resistor pull_resistor_51 (.node(controlled_buffer_3_out[39]));
  Pull_Resistor pull_resistor_52 (.node(controlled_buffer_3_out[40]));
  Pull_Resistor pull_resistor_53 (.node(controlled_buffer_3_out[41]));
  Pull_Resistor pull_resistor_54 (.node(controlled_buffer_3_out[42]));
  Pull_Resistor pull_resistor_55 (.node(controlled_buffer_3_out[43]));
  Pull_Resistor pull_resistor_56 (.node(controlled_buffer_3_out[44]));
  Pull_Resistor pull_resistor_57 (.node(controlled_buffer_3_out[45]));
  Pull_Resistor pull_resistor_58 (.node(controlled_buffer_3_out[46]));
  Pull_Resistor pull_resistor_59 (.node(controlled_buffer_3_out[47]));
  Pull_Resistor pull_resistor_60 (.node(controlled_buffer_3_out[48]));
  Pull_Resistor pull_resistor_61 (.node(controlled_buffer_3_out[49]));
  Pull_Resistor pull_resistor_62 (.node(controlled_buffer_3_out[50]));
  Pull_Resistor pull_resistor_63 (.node(controlled_buffer_3_out[51]));
  Pull_Resistor pull_resistor_64 (.node(controlled_buffer_3_out[52]));
  Pull_Resistor pull_resistor_65 (.node(controlled_buffer_3_out[53]));
  Pull_Resistor pull_resistor_66 (.node(controlled_buffer_3_out[54]));
  Pull_Resistor pull_resistor_67 (.node(controlled_buffer_3_out[55]));
  Pull_Resistor pull_resistor_68 (.node(controlled_buffer_3_out[56]));
  Pull_Resistor pull_resistor_69 (.node(controlled_buffer_3_out[57]));
  Pull_Resistor pull_resistor_70 (.node(controlled_buffer_3_out[58]));
  Pull_Resistor pull_resistor_71 (.node(controlled_buffer_3_out[59]));
  Pull_Resistor pull_resistor_72 (.node(controlled_buffer_3_out[60]));
  Pull_Resistor pull_resistor_73 (.node(controlled_buffer_3_out[61]));
  Pull_Resistor pull_resistor_74 (.node(controlled_buffer_3_out[62]));
  Pull_Resistor pull_resistor_75 (.node(MC_DONE));
  or or_2 (reg0w, demultiplexer_1_out0, demultiplexer_2_out0);
  or or_3 (reg1w, demultiplexer_1_out1, demultiplexer_2_out1);
  or or_4 (reg2w, demultiplexer_1_out2, demultiplexer_2_out2);
  or or_5 (reg3w, demultiplexer_1_out3, demultiplexer_2_out3);
  or or_6 (reg4w, demultiplexer_1_out4, demultiplexer_2_out4);
  or or_7 (reg5w, demultiplexer_1_out5, demultiplexer_2_out5);
  or or_8 (reg6w, demultiplexer_1_out6, demultiplexer_2_out6);
  or or_9 (reg7w, demultiplexer_1_out7, demultiplexer_2_out7);
  or or_10 (reg8w, demultiplexer_1_out8, demultiplexer_2_out8);
  or or_11 (reg9w, demultiplexer_1_out9, demultiplexer_2_out9);
  or or_12 (reg10w, demultiplexer_1_out10, demultiplexer_2_out10);
  or or_13 (reg11w, demultiplexer_1_out11, demultiplexer_2_out11);
  or or_14 (reg12w, demultiplexer_1_out12, demultiplexer_2_out12);
  or or_15 (reg13w, demultiplexer_1_out13, demultiplexer_2_out13);
  or or_16 (reg14w, demultiplexer_1_out14, demultiplexer_2_out14);
  or or_17 (reg15w, demultiplexer_1_out15, demultiplexer_2_out15);
  and and_1 (and_1_out, clk, clk);
  Demultiplexer #(.select(4), .width(8)) demultiplexer_3 (
    .out0(demultiplexer_3_out0), .out1(demultiplexer_3_out1), .out2(demultiplexer_3_out2),
    .out3(demultiplexer_3_out3), .out4(demultiplexer_3_out4), .out5(demultiplexer_3_out5),
    .out6(demultiplexer_3_out6), .out7(demultiplexer_3_out7), .out8(demultiplexer_3_out8),
    .out9(demultiplexer_3_out9), .out10(demultiplexer_3_out10), .out11(demultiplexer_3_out11),
    .out12(demultiplexer_3_out12), .out13(demultiplexer_3_out13), .out14(demultiplexer_3_out14),
    .out15(demultiplexer_3_out15), .in(regdi2), .sel(regs2));
  Button button_2 (.out(button_2_out));
  and and_2 (and_2_out, and_1_out, MC_DONE);
  Hex_Digit_Display hex_digit_display_1 (.value(op0[7:4]));  // open: dp
  Demultiplexer #(.select(4), .width(8)) demultiplexer_4 (
    .out0(demultiplexer_4_out0), .out1(demultiplexer_4_out1), .out2(demultiplexer_4_out2),
    .out3(demultiplexer_4_out3), .out4(demultiplexer_4_out4), .out5(demultiplexer_4_out5),
    .out6(demultiplexer_4_out6), .out7(demultiplexer_4_out7), .out8(demultiplexer_4_out8),
    .out9(demultiplexer_4_out9), .out10(demultiplexer_4_out10), .out11(demultiplexer_4_out11),
    .out12(demultiplexer_4_out12), .out13(demultiplexer_4_out13), .out14(demultiplexer_4_out14),
    .out15(demultiplexer_4_out15), .in(regdi1), .sel(regs1));
  or or_18 (op_done, button_2_out, and_2_out);
  Hex_Digit_Display hex_digit_display_2 (.value(op0[3:0]));  // open: dp
  Hex_Digit_Display hex_digit_display_3 (.value(op1[7:4]));  // open: dp
  Hex_Digit_Display hex_digit_display_4 (.value(op1[3:0]));  // open: dp
  Hex_Digit_Display hex_digit_display_5 (.value(rom_1_data_2[7:4]));  // open: dp
  Counter #(.max('hffff), .trigger("falling"), .width(16)) counter_1 (
    .clr(res), .load(rip_wi), .count(1'b1), .clk(clk), .D(rip_i), .Q(rom_addr));  // open: up, carry
  Hex_Digit_Display hex_digit_display_6 (.value(rom_1_data_2[3:0]));  // open: dp
  Hex_Digit_Display hex_digit_display_7 (.value(rom_1_data_3[7:4]));  // open: dp
  Hex_Digit_Display hex_digit_display_8 (.value(rom_1_data));  // open: dp
  Hex_Digit_Display hex_digit_display_9 (.value(rom_1_data_3[3:0]));  // open: dp
  Hex_Digit_Display hex_digit_display_10 (.value(rom_1_data_4));  // open: dp
  Hex_Digit_Display hex_digit_display_11 (.value(rom_1_data_5));  // open: dp
  assign reg0d = demultiplexer_4_out0 | demultiplexer_3_out0;  // OR_Gate or_19, 8 bits wide
  assign reg1d = demultiplexer_4_out1 | demultiplexer_3_out1;  // OR_Gate or_20, 8 bits wide
  assign reg2d = demultiplexer_4_out2 | demultiplexer_3_out2;  // OR_Gate or_21, 8 bits wide
  assign reg3d = demultiplexer_4_out3 | demultiplexer_3_out3;  // OR_Gate or_22, 8 bits wide
  assign reg4d = demultiplexer_4_out4 | demultiplexer_3_out4;  // OR_Gate or_23, 8 bits wide
  assign reg5d = demultiplexer_4_out5 | demultiplexer_3_out5;  // OR_Gate or_24, 8 bits wide
  assign reg6d = demultiplexer_4_out6 | demultiplexer_3_out6;  // OR_Gate or_25, 8 bits wide
  assign reg7d = demultiplexer_4_out7 | demultiplexer_3_out7;  // OR_Gate or_26, 8 bits wide
  assign reg8d = demultiplexer_4_out8 | demultiplexer_3_out8;  // OR_Gate or_27, 8 bits wide
  assign reg9d = demultiplexer_4_out9 | demultiplexer_3_out9;  // OR_Gate or_28, 8 bits wide
  assign reg10d = demultiplexer_4_out10 | demultiplexer_3_out10;  // OR_Gate or_29, 8 bits wide
  assign reg11d = demultiplexer_4_out11 | demultiplexer_3_out11;  // OR_Gate or_30, 8 bits wide
  assign reg12d = demultiplexer_4_out12 | demultiplexer_3_out12;  // OR_Gate or_31, 8 bits wide
  assign reg13d = demultiplexer_4_out13 | demultiplexer_3_out13;  // OR_Gate or_32, 8 bits wide
  assign reg14d = demultiplexer_4_out14 | demultiplexer_3_out14;  // OR_Gate or_33, 8 bits wide
  assign reg15d = demultiplexer_4_out15 | demultiplexer_3_out15;  // OR_Gate or_34, 8 bits wide
  Hex_Digit_Display hex_digit_display_12 (.value(rom_1_data_6));  // open: dp
  Hex_Digit_Display hex_digit_display_13 (.value(rom_1_data_7));  // open: dp
  Multiplexer #(.select(4), .width(8)) multiplexer_1 (
    .in0(reg0o), .in1(reg1o), .in2(reg2o), .in3(reg3o), .in4(reg4o), .in5(reg5o), .in6(reg6o), .in7(reg7o),
    .in8(reg8o), .in9(reg9o), .in10(reg10o), .in11(reg11o), .in12(reg12o), .in13(reg13o), .in14(reg14o),
    .in15(reg15o), .out(regdo1), .sel(regs1));
  Hex_Digit_Display hex_digit_display_14 (.value(rom_1_data_8));  // open: dp
  Hex_Digit_Display hex_digit_display_15 (.value(rom_1_data_9));  // open: dp
  Pull_Resistor pull_resistor_76 (.node(rip_i));
  Pull_Resistor pull_resistor_77 (.node(rip_wi));
  Hex_Digit_Display hex_digit_display_16 (.value(rom_1_data_10));  // open: dp
  assign regs1 = MC_STR_REG_0_BUS ? 4'b0000 : 4'bz;  // Controlled_Buffer controlled_buffer_4
  assign regs1 = MC_STR_REG_1_BUS ? 4'b0001 : 4'bz;  // Controlled_Buffer controlled_buffer_5
  assign regs1 = MC_STR_REG_2_BUS ? 4'b0010 : 4'bz;  // Controlled_Buffer controlled_buffer_6
  assign regs1 = MC_STR_REG_3_BUS ? 4'b0011 : 4'bz;  // Controlled_Buffer controlled_buffer_7
  assign regs1 = MC_STR_REG_IOP0_LO_BUS ? op0[3:0] : 4'bz;  // Controlled_Buffer controlled_buffer_8
  assign regs1 = MC_STR_REG_IOP0_HI_BUS ? op0[7:4] : 4'bz;  // Controlled_Buffer controlled_buffer_9
  assign regs2 = MC_PUT_REG_IOP0_LO_BUS ? op0[3:0] : 4'bz;  // Controlled_Buffer controlled_buffer_10
  assign regs2 = MC_PUT_REG_IOP0_HI_BUS ? op0[7:4] : 4'bz;  // Controlled_Buffer controlled_buffer_11
  assign ram_addr = MC_RAM_WRITE_BUS_A ? {reg0o, reg1o} : 16'bz;  // Controlled_Buffer controlled_buffer_12
  assign ram_addr = MC_RAM_WRITE_BUS_B ? {reg0o, reg1o} : 16'bz;  // Controlled_Buffer controlled_buffer_13
  assign ram_addr = MC_RAM_READ_BUS_A ? {reg0o, reg1o} : 16'bz;  // Controlled_Buffer controlled_buffer_14
  assign ram_addr = MC_RAM_READ_BUS_B ? {reg0o, reg1o} : 16'bz;  // Controlled_Buffer controlled_buffer_15
  assign io_addr = MC_IO_WRITE_BUS_A ? {reg0o, reg1o} : 16'bz;  // Controlled_Buffer controlled_buffer_16
  assign io_addr = MC_IO_WRITE_BUS_B ? {reg0o, reg1o} : 16'bz;  // Controlled_Buffer controlled_buffer_17
  assign io_addr = MC_IO_READ_BUS_A ? {reg0o, reg1o} : 16'bz;  // Controlled_Buffer controlled_buffer_18
  assign io_addr = MC_IO_READ_BUS_B ? {reg0o, reg1o} : 16'bz;  // Controlled_Buffer controlled_buffer_19
  Multiplexer #(.select(4), .width(8)) multiplexer_2 (
    .in0(reg0o), .in1(reg1o), .in2(reg2o), .in3(reg3o), .in4(reg4o), .in5(reg5o), .in6(reg6o), .in7(reg7o),
    .in8(reg8o), .in9(reg9o), .in10(reg10o), .in11(reg11o), .in12(reg12o), .in13(reg13o), .in14(reg14o),
    .in15(reg15o), .out(regdo2), .sel(regs2));
  or or_35 (ram_save, MC_RAM_WRITE_BUS_A, MC_RAM_WRITE_BUS_B);
  or or_36 (or_36_out, MC_RAM_READ_BUS_A, MC_RAM_READ_BUS_B);
  or or_37 (io_save, MC_IO_WRITE_BUS_A, MC_IO_WRITE_BUS_B);
  or or_38 (or_38_out, MC_IO_READ_BUS_A, MC_IO_READ_BUS_B);
  assign alu0d = alu0w ? data_bus : 8'bz;  // Controlled_Buffer controlled_buffer_20
  assign alu1d = alu1w ? data_bus : 8'bz;  // Controlled_Buffer controlled_buffer_21
  or or_39 (regwi1, MC_STR_REG_0_BUS, MC_STR_REG_1_BUS, MC_STR_REG_2_BUS, MC_STR_REG_3_BUS, MC_STR_REG_IOP0_LO_BUS, MC_STR_REG_IOP0_HI_BUS);
  or or_40 (or_40_out, MC_PUT_REG_IOP0_LO_BUS, MC_PUT_REG_IOP0_HI_BUS);
  Register #(.trigger("falling")) register_1 (.D(reg0d), .en(reg0w), .clk(clk), .Q(reg0o), .clr(res));
  Hex_Digit_Display hex_digit_display_17 (.value(data_bus[7:4]));  // open: dp
  Hex_Digit_Display hex_digit_display_18 (.value(data_bus[3:0]));  // open: dp
  Pull_Resistor pull_resistor_78 (.node(data_bus));
  Hex_Digit_Display hex_digit_display_19 (.value(op0[3:0]));  // open: dp
  assign data_bus = or_40_out ? regdo2 : 8'bz;  // Controlled_Buffer controlled_buffer_22
  assign ram_in = ram_save ? data_bus : 8'bz;  // Controlled_Buffer controlled_buffer_23
  assign data_bus = or_36_out ? ram_out : 8'bz;  // Controlled_Buffer controlled_buffer_24
  assign io_in = io_save ? data_bus : 8'bz;  // Controlled_Buffer controlled_buffer_25
  assign data_bus = or_38_out ? io_out : 8'bz;  // Controlled_Buffer controlled_buffer_26
  Hex_Digit_Display hex_digit_display_20 (.value(reg0o[7:4]));  // open: dp
  Hex_Digit_Display hex_digit_display_21 (.value(reg0o[3:0]));  // open: dp
  Hex_Digit_Display hex_digit_display_22 (.value(reg0o[7:4]));  // open: dp
  Hex_Digit_Display hex_digit_display_23 (.value(reg0o[3:0]));  // open: dp
  Hex_Digit_Display hex_digit_display_24 (.value(reg2o[7:4]));  // open: dp
  Hex_Digit_Display hex_digit_display_25 (.value(reg2o[3:0]));  // open: dp
  assign regdi1 = regwi1 ? data_bus : 8'bz;  // Controlled_Buffer controlled_buffer_27
  Hex_Digit_Display hex_digit_display_26 (.value(op0[7:4]));  // open: dp
  Hex_Digit_Display hex_digit_display_27 (.value(reg1o[7:4]));  // open: dp
  Hex_Digit_Display hex_digit_display_28 (.value(reg1o[3:0]));  // open: dp
  Hex_Digit_Display hex_digit_display_29 (.value(reg3o[7:4]));  // open: dp
  Hex_Digit_Display hex_digit_display_30 (.value(reg3o[3:0]));  // open: dp
  Hex_Digit_Display hex_digit_display_31 (.value(alu0o[7:4]));  // open: dp
  assign data_bus = MC_PUT_VAL_IOP0_BUS ? op0 : 8'bz;  // Controlled_Buffer controlled_buffer_28
  assign data_bus = MC_PUT_VAL_IOP1_BUS ? op1 : 8'bz;  // Controlled_Buffer controlled_buffer_29
  Hex_Digit_Display hex_digit_display_32 (.value(data_bus[7:4]));  // open: dp
  Hex_Digit_Display hex_digit_display_33 (.value(data_bus[3:0]));  // open: dp
  Hex_Digit_Display hex_digit_display_34 (.value(ram_addr[15:12]));  // open: dp
  Hex_Digit_Display hex_digit_display_35 (.value(ram_addr[11:8]));  // open: dp
  Hex_Digit_Display hex_digit_display_36 (.value(io_addr[15:12]));  // open: dp
  Hex_Digit_Display hex_digit_display_37 (.value(io_in[7:4]));  // open: dp
  Register #(.trigger("falling")) register_2 (.D(reg1d), .en(reg1w), .clk(clk), .Q(reg1o), .clr(res));
  Hex_Digit_Display hex_digit_display_38 (.value(reg1o[7:4]));  // open: dp
  Hex_Digit_Display hex_digit_display_39 (.value(reg1o[3:0]));  // open: dp
  Hex_Digit_Display hex_digit_display_40 (.value(alu0o[3:0]));  // open: dp
  Pull_Resistor pull_resistor_79 (.node(alu0o));
  Pull_Resistor pull_resistor_80 (.node(data_bus));
  Hex_Digit_Display hex_digit_display_41 (.value(ram_addr[7:4]));  // open: dp
  Hex_Digit_Display hex_digit_display_42 (.value(ram_addr[3:0]));  // open: dp
  Hex_Digit_Display hex_digit_display_43 (.value(io_addr[11:8]));  // open: dp
  Hex_Digit_Display hex_digit_display_44 (.value(io_addr[7:4]));  // open: dp
  Hex_Digit_Display hex_digit_display_45 (.value(io_in[3:0]));  // open: dp
  Hex_Digit_Display hex_digit_display_46 (.value(alu1o[7:4]));  // open: dp
  Hex_Digit_Display hex_digit_display_47 (.value(alu1o[3:0]));  // open: dp
  Hex_Digit_Display hex_digit_display_48 (.value(io_addr[3:0]));  // open: dp
  Register #(.trigger("falling")) register_3 (.D(reg2d), .en(reg2w), .clk(clk), .Q(reg2o), .clr(res));
  Hex_Digit_Display hex_digit_display_49 (.value(reg2o[7:4]));  // open: dp
  Hex_Digit_Display hex_digit_display_50 (.value(reg2o[3:0]));  // open: dp
  Pull_Resistor pull_resistor_81 (.node(alu1o));
  Hex_Digit_Display hex_digit_display_51 (.value(ram_in[7:4]));  // open: dp
  Hex_Digit_Display hex_digit_display_52 (.value(ram_out[7:4]));  // open: dp
  Hex_Digit_Display hex_digit_display_53 (.value(io_out[7:4]));  // open: dp
  Hex_Digit_Display hex_digit_display_54 (.value(io_out[3:0]));  // open: dp
  Hex_Digit_Display hex_digit_display_55 (.value(alu_out[7:4]));  // open: dp
  Hex_Digit_Display hex_digit_display_56 (.value(alu_out[3:0]));  // open: dp
  Pull_Resistor pull_resistor_82 (.node(alu_out));
  Register #(.trigger("falling")) register_4 (.D(alu0d), .en(alu0w), .clk(clk), .Q(alu0o), .clr(res));
  Hex_Digit_Display hex_digit_display_57 (.value(ram_in[3:0]));  // open: dp
  Pull_Resistor pull_resistor_83 (.node(ram_in));
  Hex_Digit_Display hex_digit_display_58 (.value(ram_out[3:0]));  // open: dp
  Pull_Resistor pull_resistor_84 (.node(ram_out));
  Register #(.trigger("falling")) register_5 (.D(reg3d), .en(reg3w), .clk(clk), .Q(reg3o), .clr(res));
  Hex_Digit_Display hex_digit_display_59 (.value(reg3o[7:4]));  // open: dp
  Hex_Digit_Display hex_digit_display_60 (.value(reg3o[3:0]));  // open: dp
  Register #(.trigger("falling")) register_6 (.D(alu1d), .en(alu1w), .clk(clk), .Q(alu1o), .clr(res));
  assign and_3_out = alu0o & alu1o;  // AND_Gate and_3, 8 bits wide
  assign alu_out = MC_ALU_AND ? and_3_out : 8'bz;  // Controlled_Buffer controlled_buffer_30
  assign or_41_out = alu0o | alu1o;  // OR_Gate or_41, 8 bits wide
  assign alu_out = MC_ALU_OR ? or_41_out : 8'bz;  // Controlled_Buffer controlled_buffer_31
  Register #(.trigger("falling")) register_7 (.D(reg4d), .en(reg4w), .clk(clk), .Q(reg4o), .clr(res));
  Hex_Digit_Display hex_digit_display_61 (.value(reg4o[7:4]));  // open: dp
  RAM #(.addrWidth(16), .enables("line"), .trigger("falling")) ram_1 (
    .addr(ram_addr), .we(ram_save), .oe(clk), .clk(clk), .din(ram_in), .dout(ram_out));
  and and_4 (and_4_out, MC_ALU_ADD_OV, alu_flag_ov_o);
  and and_5 (and_5_out, MC_ALU_SUB_OV, alu_flag_ov_o);
  Hex_Digit_Display hex_digit_display_62 (.value(reg4o[3:0]));  // open: dp
  or or_42 (or_42_out, MC_ALU_ADD, MC_ALU_ADD_OV);
  Adder adder_1 (.a(alu0o), .b(alu1o), .out(adder_1_out), .cin(and_4_out), .cout(adder_1_cout));
  Pull_Resistor pull_resistor_85 (.node(adder_1_cout));
  or or_43 (or_43_out, MC_ALU_SUB, MC_ALU_SUB_OV);
  Subtractor subtractor_1 (.a(alu0o), .b(alu1o), .out(subtractor_1_out), .bin(and_5_out), .bout(subtractor_1_bout));
  Pull_Resistor pull_resistor_86 (.node(subtractor_1_bout));
  assign data_bus = MC_PUT_ALU_RES_BUS ? alu_out : 8'bz;  // Controlled_Buffer controlled_buffer_32
  Register #(.trigger("falling")) register_8 (.D(reg5d), .en(reg5w), .clk(clk), .Q(reg5o), .clr(res));
  Hex_Digit_Display hex_digit_display_63 (.value(reg5o[7:4]));  // open: dp
  Pull_Resistor pull_resistor_87 (.node(alu0d));
  Pull_Resistor pull_resistor_88 (.node(alu0w));
  Pull_Resistor pull_resistor_89 (.node(alu0o));
  Pull_Resistor pull_resistor_90 (.node(alu_out));
  assign alu_out = or_42_out ? adder_1_out : 8'bz;  // Controlled_Buffer controlled_buffer_33
  assign alu_flag_ov_i = or_42_out ? adder_1_cout : 1'bz;  // Controlled_Buffer controlled_buffer_34
  assign alu_out = or_43_out ? subtractor_1_out : 8'bz;  // Controlled_Buffer controlled_buffer_35
  assign alu_flag_ov_i = or_43_out ? subtractor_1_bout : 1'bz;  // Controlled_Buffer controlled_buffer_36
  assign not_2_out = ~alu0o;  // NOT_Gate not_2, 8 bits wide
  assign alu_out = MC_ALU_NOT ? not_2_out : 8'bz;  // Controlled_Buffer controlled_buffer_37
  Pull_Resistor pull_resistor_91 (.node(pull_resistor_91_node));
  assign alu_flag_eq_i = alu_flag_eq_wi ? pull_resistor_91_node : 1'bz;  // Controlled_Buffer controlled_buffer_38
  Comparator comparator_1 (.a(alu0o), .b(alu1o), .eq(pull_resistor_91_node));  // open: gt, lt
  Hex_Digit_Display hex_digit_display_64 (.value(reg5o[3:0]));  // open: dp
  Pull_Resistor pull_resistor_92 (.node(alu1d));
  Pull_Resistor pull_resistor_93 (.node(alu1w));
  Pull_Resistor pull_resistor_94 (.node(alu1o));
  Register #(.trigger("falling")) register_9 (.D(reg6d), .en(reg6w), .clk(clk), .Q(reg6o), .clr(res));
  Hex_Digit_Display hex_digit_display_65 (.value(reg6o[7:4]));  // open: dp
  or or_44 (alu_flag_ov_wi, or_42_out, or_43_out);
  and and_6 (and_6_out, MC_JEQ, alu_flag_eq_o);
  not not_3 (not_3_out, alu_flag_eq_o);
  and and_7 (and_7_out, MC_JNEQ, not_3_out);
  or or_45 (rip_wi, MC_JMP, and_6_out, and_7_out);
  assign rip_i = rip_wi ? {op0, op1} : 16'bz;  // Controlled_Buffer controlled_buffer_39
  Hex_Digit_Display hex_digit_display_66 (.value(reg6o[3:0]));  // open: dp
  Register #(.trigger("falling")) register_10 (.D(reg7d), .en(reg7w), .clk(clk), .Q(reg7o), .clr(res));
  Hex_Digit_Display hex_digit_display_67 (.value(reg7o[7:4]));  // open: dp
  Hex_Digit_Display hex_digit_display_68 (.value(reg7o[3:0]));  // open: dp
  Pull_Resistor pull_resistor_95 (.node(ram_in));
  Pull_Resistor pull_resistor_96 (.node(ram_save));
  Pull_Resistor pull_resistor_97 (.node(ram_addr));
  Pull_Resistor pull_resistor_98 (.node(ram_out));
  Register #(.trigger("falling")) register_11 (.D(reg8d), .en(reg8w), .clk(clk), .Q(reg8o), .clr(res));
  Hex_Digit_Display hex_digit_display_69 (.value(op0[7:4]));  // open: dp
  Hex_Digit_Display hex_digit_display_70 (.value(op0[3:0]));  // open: dp
  Pull_Resistor pull_resistor_99 (.node(op0));
  Hex_Digit_Display hex_digit_display_71 (.value(op0[7:4]));  // open: dp
  Hex_Digit_Display hex_digit_display_72 (.value(op0[3:0]));  // open: dp
  Hex_Digit_Display hex_digit_display_73 (.value(reg8o[7:4]));  // open: dp
  Hex_Digit_Display hex_digit_display_74 (.value(reg8o[3:0]));  // open: dp
  Hex_Digit_Display hex_digit_display_75 (.value(op1[7:4]));  // open: dp
  Hex_Digit_Display hex_digit_display_76 (.value(op1[7:4]));  // open: dp
  Hex_Digit_Display hex_digit_display_77 (.value(op1[3:0]));  // open: dp
  assign io_out = io_addr[15] ? 8'hab : 8'bz;  // Controlled_Buffer controlled_buffer_40
  Hex_Digit_Display hex_digit_display_78 (.value(op1[3:0]));  // open: dp
  Pull_Resistor pull_resistor_100 (.node(op1));
  Register #(.trigger("falling")) register_12 (.D(reg9d), .en(reg9w), .clk(clk), .Q(reg9o), .clr(res));
  Hex_Digit_Display hex_digit_display_79 (.value(reg9o[7:4]));  // open: dp
  Hex_Digit_Display hex_digit_display_80 (.value(reg9o[3:0]));  // open: dp
  Pull_Resistor pull_resistor_101 (.node(alu_flag_ov_o));
  Pull_Resistor pull_resistor_102 (.node(alu_flag_eq_o));
  Pull_Resistor pull_resistor_103 (.node(alu_flag_hlt_o));
  or or_46 (or_46_out, res, MC_ALU_FLAG_RES);
  Register #(.trigger("falling")) register_13 (.D(reg10d), .en(reg10w), .clk(clk), .Q(reg10o), .clr(res));
  Hex_Digit_Display hex_digit_display_81 (.value(reg10o[7:4]));  // open: dp
  Hex_Digit_Display hex_digit_display_82 (.value(reg10o[3:0]));  // open: dp
  Register #(.trigger("falling"), .width(1)) register_14 (
    .D(alu_flag_ov_i), .en(alu_flag_ov_wi), .clk(clk), .Q(alu_flag_ov_o), .clr(or_46_out));
  Register #(.trigger("falling"), .width(1)) register_15 (
    .D(alu_flag_eq_i), .en(alu_flag_eq_wi), .clk(clk), .Q(alu_flag_eq_o), .clr(or_46_out));
  Register #(.trigger("falling"), .width(1)) register_16 (
    .D(alu_flag_hlt_i), .en(alu_flag_hlt_i), .clk(clk), .Q(alu_flag_hlt_o), .clr(or_46_out));
  Pull_Resistor pull_resistor_104 (.node(io_addr));
  Pull_Resistor pull_resistor_105 (.node(io_in));
  Pull_Resistor pull_resistor_106 (.node(io_out));
  Pull_Resistor pull_resistor_107 (.node(io_save));
  Pull_Resistor pull_resistor_108 (.node(alu_flag_ov_i));
  Pull_Resistor pull_resistor_109 (.node(alu_flag_eq_i));
  Pull_Resistor pull_resistor_110 (.node(alu_flag_hlt_i));
  Register #(.trigger("falling")) register_17 (.D(reg11d), .en(reg11w), .clk(clk), .Q(reg11o), .clr(res));
  Hex_Digit_Display hex_digit_display_83 (.value(reg11o[7:4]));  // open: dp
  Pull_Resistor pull_resistor_111 (.node(alu_flag_hlt_i));
  Pull_Resistor pull_resistor_112 (.node(alu_flag_eq_wi));
  Pull_Resistor pull_resistor_113 (.node(alu_flag_ov_wi));
  Hex_Digit_Display hex_digit_display_84 (.value(reg11o[3:0]));  // open: dp
  Hex_Digit_Display hex_digit_display_85 (.value(io_addr[15:12]));  // open: dp
  Hex_Digit_Display hex_digit_display_86 (.value(io_addr[11:8]));  // open: dp
  Hex_Digit_Display hex_digit_display_87 (.value(io_in[7:4]));  // open: dp
  Hex_Digit_Display hex_digit_display_88 (.value(io_in[3:0]));  // open: dp
  Hex_Digit_Display hex_digit_display_89 (.value(reg12o[7:4]));  // open: dp
  Hex_Digit_Display hex_digit_display_90 (.value(io_addr[7:4]));  // open: dp
  Hex_Digit_Display hex_digit_display_91 (.value(io_addr[3:0]));  // open: dp
  Register #(.trigger("falling")) register_18 (.D(reg12d), .en(reg12w), .clk(clk), .Q(reg12o), .clr(res));
  Hex_Digit_Display hex_digit_display_92 (.value(reg12o[3:0]));  // open: dp
  Hex_Digit_Display hex_digit_display_93 (.value(io_out[7:4]));  // open: dp
  Hex_Digit_Display hex_digit_display_94 (.value(io_out[3:0]));  // open: dp
  Register #(.trigger("falling")) register_19 (.D(reg13d), .en(reg13w), .clk(clk), .Q(reg13o), .clr(res));
  Hex_Digit_Display hex_digit_display_95 (.value(reg13o[7:4]));  // open: dp
  Hex_Digit_Display hex_digit_display_96 (.value(reg13o[3:0]));  // open: dp
  Register #(.trigger("falling")) register_20 (.D(reg14d), .en(reg14w), .clk(clk), .Q(reg14o), .clr(res));
  Hex_Digit_Display hex_digit_display_97 (.value(reg14o[7:4]));  // open: dp
  Hex_Digit_Display hex_digit_display_98 (.value(reg14o[3:0]));  // open: dp
  Hex_Digit_Display hex_digit_display_99 (.value(reg15o[7:4]));  // open: dp
  Register #(.trigger("falling")) register_21 (.D(reg15d), .en(reg15w), .clk(clk), .Q(reg15o), .clr(res));
  Hex_Digit_Display hex_digit_display_100 (.value(reg15o[3:0]));  // open: dp

  // Other names for the same wires on the sheet: MC_STR_ALU_REG_0_BUS = alu0w; MC_STR_ALU_REG_1_BUS = alu1w;
  //   MC_ALU_CMP = alu_flag_eq_wi; alu_flag_hlt_wi = alu_flag_hlt_i; MC_HLT = alu_flag_hlt_i; exec_op = clk;
  //   op_mixed[15:0] = {op0, op1}; op0sublow[3:0] = op0[3:0]; op0subhigh[3:0] = op0[7:4];
  //   regao[15:0] = {reg0o, reg1o}; regbo[15:0] = {reg2o, reg3o}

  // Notes on the sheet:
  //   contents of rom_1 (hex, n*v repeats v):
  //   1000000040002 1000000080020 1000020100008 20000000040002 20000000080020 20000008000000 80000000
  //   100000000
  //   REGISTER INPUT COMBINERS
  //   MICROCODE ROM
  //   CLOCK + RESET
  //   REGISTER MUXERS AND DEMUXERS
  //   MICROCODE STEP
  //   INSTRUCTION SPLITTERS
  //   REGISTER COMBINATORS
  //   INSTRUCTION COUNTER
  //   DATA BUS
  //   REGISTERS
  //   DATA BUS
  //   RAM ADDR
  //   ALU REG 0
  //   ALU REG 1
  //   ALU OUT
  //   RAM IN
  //   RAM OUT
  //   ALU
  //   RAM
  //   CONTROL FLOW
  //   RAM CONTROLS
  //   TEST IO
  //   ALU FLAGS
  //   ALU FLAG OV
  //   ALU FLAG EQ
  //   ALU FLAG HLT
  //   IO CONNECTION
endmodule
